// Logisim project entrega_final_cliente_arbol.circ as structural Verilog: 1 circuit, main circuit main
module main (
);

  wire breadboard_1_p1, clock_chip_1_p3, flipflopchip_1_p1, flipflopchip_1_p4, flipflopchip_1_p5,
       flipflopchip_1_p7, flipflopchip_2_p1, flipflopchip_2_p2, flipflopchip_2_p5, flipflopchip_2_p7,
       flipflopchip_2_p9, flipflopchip_2_p11, protosimandchip_1_p1, protosimandchip_1_p3,
       protosimandchip_1_p6, protosimandchip_1_p8, protosimandchip_1_p10, protosimandchip_1_p12,
       protosimandchip_1_p13, protosimandchip_2_p1, protosimandchip_2_p3, protosimandchip_2_p4,
       protosimandchip_2_p5, protosimandchip_2_p7, protosimandchip_2_p10, protosimandchip_2_p12,
       protosimandchip_2_p14, protosimandchip_2_p15, protosimandchip_2_p19, protosimandchip_2_p21,
       protosimandchip_2_p22, protosimandchip_3_p1, protosimandchip_3_p2, protosimandchip_3_p4,
       protosimandchip_3_p6, protosimandchip_3_p7, protosimandchip_3_p11, protosimandchip_3_p12,
       protosimandchip_4_p1, protosimandchip_4_p3, protosimandchip_4_p4, protosimandchip_4_p5,
       protosimandchip_4_p7, protosimandchip_4_p11, protosimandchip_4_p14, protosimandchip_4_p15,
       protosimnotchip_1_p1, protosimnotchip_1_p3, protosimnotchip_1_p5, protosimnotchip_1_p8,
       protosimnotchip_1_p10, protosimnotchip_1_p11, protosimnotchip_1_p12, protosimnotchip_1_p14,
       protosimnotchip_1_p15, voltagegenerator_1_p1, voltagegenerator_1_p2;

  // VoltageGenerator voltagegenerator_1: pin names not known; wires that end beside it: voltagegenerator_1_p1, voltagegenerator_1_p2
  // Breadboard breadboard_1: pin names not known; wires that end beside it: breadboard_1_p1
  // Clock_Chip clock_chip_1: pin names not known; wires that end beside it: voltagegenerator_1_p1, voltagegenerator_1_p2, clock_chip_1_p3
  // FlipFlopChip flipflopchip_1: pin names not known; wires that end beside it: flipflopchip_1_p1, flipflopchip_1_p1, breadboard_1_p1, flipflopchip_1_p4, flipflopchip_1_p5, clock_chip_1_p3, flipflopchip_1_p7
  // FlipFlopChip flipflopchip_2: pin names not known; wires that end beside it: flipflopchip_2_p1, flipflopchip_2_p2, flipflopchip_1_p7, flipflopchip_1_p4, flipflopchip_2_p5, flipflopchip_1_p5, flipflopchip_2_p7, flipflopchip_2_p7, flipflopchip_2_p9, flipflopchip_2_p9, flipflopchip_2_p11, flipflopchip_2_p5
  // ProtosimNotChip protosimnotchip_1: pin names not known; wires that end beside it: protosimnotchip_1_p1, flipflopchip_2_p11, protosimnotchip_1_p3, protosimnotchip_1_p3, protosimnotchip_1_p5, protosimnotchip_1_p5, flipflopchip_2_p1, protosimnotchip_1_p8, protosimnotchip_1_p1, protosimnotchip_1_p10, protosimnotchip_1_p11, protosimnotchip_1_p12, flipflopchip_2_p2, protosimnotchip_1_p14, protosimnotchip_1_p15
  // ProtosimAndChip protosimandchip_1: pin names not known; wires that end beside it: protosimandchip_1_p1, protosimandchip_1_p1, protosimandchip_1_p3, protosimandchip_1_p3, protosimnotchip_1_p12, protosimandchip_1_p6, protosimnotchip_1_p12, protosimandchip_1_p8, protosimnotchip_1_p15, protosimandchip_1_p10, protosimnotchip_1_p14, protosimandchip_1_p12, protosimandchip_1_p13, protosimandchip_1_p12, protosimandchip_1_p13
  // ProtosimAndChip protosimandchip_2: pin names not known; wires that end beside it: protosimandchip_2_p1, protosimnotchip_1_p11, protosimandchip_2_p3, protosimandchip_2_p4, protosimandchip_2_p5, protosimandchip_2_p5, protosimandchip_2_p7, protosimandchip_2_p7, protosimandchip_1_p6, protosimandchip_2_p10, protosimnotchip_1_p10, protosimandchip_2_p12, protosimandchip_1_p8, protosimandchip_2_p14, protosimandchip_2_p15, protosimandchip_2_p14, protosimandchip_2_p15, protosimnotchip_1_p8, protosimandchip_2_p19, protosimandchip_2_p1, protosimandchip_2_p21, protosimandchip_2_p22
  // ProtosimAndChip protosimandchip_3: pin names not known; wires that end beside it: protosimandchip_3_p1, protosimandchip_3_p2, protosimandchip_3_p2, protosimandchip_3_p4, protosimandchip_3_p4, protosimandchip_3_p6, protosimandchip_3_p7, protosimandchip_2_p10, protosimandchip_3_p7, protosimandchip_2_p12, protosimandchip_3_p11, protosimandchip_3_p12, protosimandchip_3_p11, protosimandchip_3_p12, protosimandchip_2_p21
  // ProtosimAndChip protosimandchip_4: pin names not known; wires that end beside it: protosimandchip_4_p1, protosimandchip_2_p19, protosimandchip_4_p3, protosimandchip_4_p4, protosimandchip_4_p5, protosimandchip_4_p5, protosimandchip_4_p7, protosimandchip_4_p7, protosimandchip_3_p6, protosimandchip_1_p10, protosimandchip_4_p11, protosimandchip_4_p11, protosimandchip_4_p1, protosimandchip_4_p14, protosimandchip_4_p15, protosimandchip_4_p15, {32{1'b0}}, {32{1'b0}}
  LED led_1 (.in(protosimandchip_4_p3));
  // LED led_2: pin names not known; wires that end beside it: {32{1'b0}}, {32{1'b0}}
  // LED led_3: pin names not known; wires that end beside it: {32{1'b0}}, {32{1'b0}}, {32{1'b0}}, {32{1'b0}}
  LED led_4 (.in(protosimandchip_3_p1));
  LED led_5 (.in(1'b0));
  // LED led_6: pin names not known; wires that end beside it: {32{1'b0}}, {32{1'b0}}
  LED led_7 ();  // open: in
  LED led_8 ();  // open: in
  LED led_9 ();  // open: in
  LED led_10 (.in(1'b0));
  LED led_11 (.in(1'b0));
  // LED led_12: pin names not known; wires that end beside it: {32{1'b0}}, {32{1'b0}}
  // LED led_13: pin names not known; wires that end beside it: {32{1'b0}}, {32{1'b0}}, {32{1'b0}}, {32{1'b0}}
  // LED led_14: pin names not known; wires that end beside it: {32{1'b0}}, {32{1'b0}}, protosimandchip_4_p4, {32{1'b0}}, protosimandchip_3_p1
  LED led_15 (.in(1'b0));
  LED led_16 (.in(1'b0));
  LED led_17 (.in(1'b0));
  // LED led_18: pin names not known; wires that end beside it: {32{1'b0}}, {32{1'b0}}, protosimandchip_2_p22, {32{1'b0}}, {32{1'b0}}
  // LED led_19: pin names not known; wires that end beside it: protosimandchip_2_p22, {32{1'b0}}, {32{1'b0}}, {32{1'b0}}, {32{1'b0}}
  LED led_20 (.in(1'b0));
  LED led_21 (.in(1'b0));
  LED led_22 (.in(1'b0));
  LED led_23 ();  // open: in
  LED led_24 (.in(1'b0));
  LED led_25 ();  // open: in
  // LED led_26: pin names not known; wires that end beside it: {32{1'b0}}, {32{1'b0}}, protosimandchip_2_p22, {32{1'b0}}, protosimandchip_2_p4
  LED led_27 (.in(1'b0));
  LED led_28 (.in(1'b0));
  // Pins of 1 and 32 bits meet at {32{1'b0}}

  // Notes on the sheet:
  //   ENTREGA FINAL AL CLIENTE
  //   EQUIPO LOGISIM
  //   INGENIERIA DE SOFTWARE 2015
endmodule
