// Logisim project test_32.zip.circ as structural Verilog: 1 circuit, main circuit main
module main (
  input  [31:0] in_1,
  input  [31:0] in_2,
  output [31:0] out_3,
  output [31:0] out_4
);

  wire voltagegenerator_1_p1, voltagegenerator_1_p2;

  // VoltageGenerator #(.ID(1)) voltagegenerator_1: pin names not known; wires that end beside it: voltagegenerator_1_p1, voltagegenerator_1_p2
  // NAND_Chip nand_chip_1: pin names not known; wires that end beside it: voltagegenerator_1_p2, in_2, in_1, out_3
  // ProtosimAndChip protosimandchip_1: pin names not known; wires that end beside it: voltagegenerator_1_p1, voltagegenerator_1_p2, in_2, in_1, out_4, voltagegenerator_1_p1
endmodule
