// Logisim project test_32_led.zip.circ as structural Verilog: 1 circuit, main circuit main
module main (
);

  wire nand_chip_1_p2, nand_chip_1_p4, protosimandchip_1_p5, voltagegenerator_1_p1;

  // VoltageGenerator #(.ID(1)) voltagegenerator_1: pin names not known; wires that end beside it: voltagegenerator_1_p1
  // NAND_Chip nand_chip_1: pin names not known; wires that end beside it: voltagegenerator_1_p1, nand_chip_1_p2, voltagegenerator_1_p1, nand_chip_1_p4
  // ProtosimAndChip protosimandchip_1: pin names not known; wires that end beside it: nand_chip_1_p2, voltagegenerator_1_p1, nand_chip_1_p2, voltagegenerator_1_p1, protosimandchip_1_p5, nand_chip_1_p2, nand_chip_1_p4, protosimandchip_1_p5
  LED #(.ID(2)) led_1 ();  // open: in
endmodule
