// Logisim project Prueba1.circ as structural Verilog: 1 circuit, main circuit main
module main (
  input  in_1,
  input  in_2,
  output [31:0] out_3
);

  wire voltagegenerator_1_p1, voltagegenerator_2_p1;

  // VoltageGenerator voltagegenerator_1: pin names not known; wires that end beside it: voltagegenerator_1_p1
  // Breadboard breadboard_1: pin names not known; wires that end beside it: in_1, in_2
  LED led_1 ();  // open: in
  // VoltageGenerator voltagegenerator_2: pin names not known; wires that end beside it: voltagegenerator_2_p1
  // ProtosimAndChip protosimandchip_1: pin names not known; wires that end beside it: voltagegenerator_1_p1, voltagegenerator_2_p1, out_3
endmodule
