// Logisim project Prueba_And.circ as structural Verilog: 1 circuit, main circuit main
module main (
);

  wire breadboard_1_p1, breadboard_1_p2, protosimandchip_1_p1, protosimandchip_1_p3, protosimandchip_1_p5,
       protosimandchip_1_p7, protosimandchip_1_p8, protosimandchip_1_p9;

  // VoltageGenerator voltagegenerator_1: pin names not known
  // Breadboard breadboard_1: pin names not known; wires that end beside it: breadboard_1_p1, breadboard_1_p2, breadboard_1_p1, breadboard_1_p2
  LED led_1 ();  // open: in
  // ProtosimAndChip protosimandchip_1: pin names not known; wires that end beside it: protosimandchip_1_p1, protosimandchip_1_p1, protosimandchip_1_p3, protosimandchip_1_p3, protosimandchip_1_p5, protosimandchip_1_p5, protosimandchip_1_p7, protosimandchip_1_p8, protosimandchip_1_p9, protosimandchip_1_p9, protosimandchip_1_p8, protosimandchip_1_p7
endmodule
