// Logisim project demofinal.circ as structural Verilog: 1 circuit, main circuit main
module main (
);

  wire and_1_out, and_2_out, and_3_out, and_4_out, and_5_out, and_6_out, and_7_out, clock_1_out, not_1_out,
       not_2_out, not_3_out;
  wire [2:0] counter_1_q;

  Clock clock_1 (.out(clock_1_out));
  Counter #(.width(3), .max('h7)) counter_1 (.Q(counter_1_q), .clk(clock_1_out));  // open: load, D, count, carry, clr
  not not_1 (not_1_out, counter_1_q[2]);
  not not_2 (not_2_out, counter_1_q[1]);
  not not_3 (not_3_out, counter_1_q[0]);
  and and_1 (and_1_out, not_1_out, not_2_out, counter_1_q[0]);
  and and_2 (and_2_out, not_1_out, counter_1_q[1], not_3_out);
  and and_3 (and_3_out, not_1_out, counter_1_q[1], counter_1_q[0]);
  and and_4 (and_4_out, counter_1_q[2], not_2_out, not_3_out);
  and and_5 (and_5_out, counter_1_q[2], not_2_out, counter_1_q[0]);
  and and_6 (and_6_out, counter_1_q[2], counter_1_q[1], not_3_out);
  and and_7 (and_7_out, counter_1_q[2], counter_1_q[1], counter_1_q[0]);
  LED led_1 (.in(and_7_out));
  LED led_2 (.in(and_7_out));
  LED led_3 (.in(and_7_out));
  LED led_4 (.in(and_7_out));
  LED led_5 (.in(and_7_out));
  LED led_6 (.in(and_7_out));
  LED led_7 (.in(and_7_out));
  LED led_8 (.in(and_5_out));
  LED led_9 (.in(and_6_out));
  LED led_10 (.in(and_5_out));
  LED led_11 (.in(and_6_out));
  LED led_12 (.in(and_6_out));
  LED led_13 (.in(and_5_out));
  LED led_14 (.in(and_6_out));
  LED led_15 (.in(and_5_out));
  LED led_16 (.in(and_6_out));
  LED led_17 (.in(and_5_out));
  LED led_18 (.in(and_5_out));
  LED led_19 (.in(and_6_out));
  LED led_20 (.in(and_5_out));
  LED led_21 (.in(and_6_out));
  LED led_22 (.in(and_4_out));
  LED led_23 (.in(and_3_out));
  LED led_24 (.in(and_4_out));
  LED led_25 (.in(and_3_out));
  LED led_26 (.in(and_4_out));
  LED led_27 (.in(and_3_out));
  LED led_28 (.in(and_3_out));
  LED led_29 (.in(and_4_out));
  LED led_30 (.in(and_3_out));
  LED led_31 (.in(and_4_out));
  LED led_32 (.in(and_4_out));
  LED led_33 (.in(and_3_out));
  LED led_34 (.in(and_4_out));
  LED led_35 (.in(and_3_out));
  LED led_36 (.in(and_2_out));
  LED led_37 (.in(and_1_out));
  LED led_38 (.in(and_2_out));
  LED led_39 (.in(and_1_out));
  LED led_40 (.in(and_1_out));
  LED led_41 (.in(and_2_out));
  LED led_42 (.in(and_1_out));
  LED led_43 (.in(and_2_out));
  LED led_44 (.in(and_2_out));
  LED led_45 (.in(and_1_out));
  LED led_46 (.in(and_2_out));
  LED led_47 (.in(and_1_out));
  LED led_48 (.in(and_1_out));
  LED led_49 (.in(and_2_out));
endmodule
